# Fritzing sketch capture_point (saved by Fritzing 0.9.3b)

parts:
  Часть1 = Arduino Nano (Rev3.0)
  S1 = Pushbutton [package="[THT]"]
  S2 = Pushbutton [package="[THT]"]
  BAT1 = BC9VPC [package=bc9vpc]
  U1 = LCD-16X2 [package=lcd-16x2]  # not connected
  R1 = Resistor [tolerance=±5% resistance=220 package=THT]
  R2 = Resistor [tolerance=±5% resistance=220 package=THT]
  LED1 = LED - 5mm [color="Yellow (595nm)" package="5 mm [THT]"]
  LED2 = LED - 5mm [color="Blue (430nm)" package="5 mm [THT]"]

nets:
  N1: Часть1.GND, S1.Pin_1, S1.Pin_2, S2.Pin_1, LED1.cathode, LED2.cathode
  N2: Часть1.D7, S1.Pin_3, S1.Pin_4
  N3: Часть1.D8, S2.Pin_3, S2.Pin_4
  N4: Часть1.D9, R1.Pin_1
  N5: Часть1.D10, R2.Pin_1
  N6: Часть1.VIN, BAT1.V+

notes:
  SDA
  SCL
  GND
  VCC
